# Fritzing sketch Cytis (saved by Fritzing 0.9.9b)

parts:
  Part1 = Arduino Nano (Rev3.0)
  L1 = Solenoid
  L298N1 = L298N DC motor driver
  L2 = Solenoid
  Part3 = Soil Moisture Sensor
  Part2 = Bluetooth HM-10
  R1 = Resistor [tolerance=±5% power=0.25 resistance=2.2k package=THT]
  R2 = Resistor [tolerance=±5% power=0.25 resistance=4.7k package=THT]
  JP1 = Header 11 [package=1x11_smd_no_holes]
  JP2 = Header 11 [package=1x11_smd_no_holes]
  VCC1 = Battery block 9V

nets:
  N1: Part1.GND, JP2.1
  N2: Part1.D2, L298N1.IN1
  N3: Part1.D3, L298N1.IN2
  N4: Part1.D4, L298N1.IN3
  N5: Part1.D5, L298N1.IN4
  N6: Part1.D6, Part2.TXD
  N7: Part1.D7, R1.Pin_1, R2.Pin_1
  VIN: Part1.VIN, L298N1.12V, VCC1.+
  N8: Part1.5V, JP1.2
  N9: Part1.A0, Part3.SIG
  N10: L1.pin1, L298N1.OUT2
  N11: L1.pin2, L298N1.OUT1
  N12: L298N1.OUT3, L2.pin1
  N13: L298N1.OUT4, L2.pin2
  N14: L298N1.GND, JP2.2, VCC1.-
  N15: L298N1.5V#7, JP1.3
  N16: L298N1.5V#9, L298N1.ENA
  N17: L298N1.5V#10, L298N1.ENB
  N18: Part3.GND, JP2.3
  N19: Part3.VCC, JP1.4
  N20: Part2.RXD, R1.Pin_0
  N21: Part2.GND, R2.Pin_0, JP2.4
  N22: Part2.VCC, JP1.1

custom parts:
  L298N DC motor driver: 2x DC motor driver with 78M05 positive voltage regulator (7..35 V) L298N: max 46 V, 2 A Set 5 V Enable jumper to enable 5 V regultor (needed for the L298N) and +5 V output at screw terminal or supply external +5 V at screw terminal Set ENA and/or ENB to +5 V to enable motor permanently or supply ENA and/or ENB with PWM signal IN1 and IN2 set rotation directory for motor A (OUT1/OUT2) IN2 and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
